# Fritzing sketch DualRGBInterface (saved by Fritzing 0.6.3b)
breadboards: 1

parts:
  Arduino1 = Arduino
  Q1 = Basic FET N-Channel [package="TO220 [THT]"]
  Q2 = Basic FET N-Channel [package="TO220 [THT]"]
  Q3 = Basic FET N-Channel [package="TO220 [THT]"]
  Q4 = Basic FET N-Channel [package="TO220 [THT]"]
  Q5 = Basic FET N-Channel [package="TO220 [THT]"]
  Q6 = Basic FET N-Channel [package="TO220 [THT]"]
  J1 = female pin header, 3 pins [form="♀ (female)"]
  J2 = female pin header, 3 pins [form="♀ (female)"]
  J3 = female pin header, 2 pins [form="♀ (female)"]

nets:
  N1: Arduino1.D11, Q1.gate
  N2: Arduino1.D10, Q2.gate
  N3: Arduino1.D9, Q3.gate
  N4: Arduino1.D6, Q6.gate
  N5: Arduino1.D5, Q5.gate
  N6: Arduino1.D3, Q4.gate
  N7: Arduino1.VIN, J3.pin1, J3.pin2
  N8: Q1.drain, J1.pin1
  GND: Q1.source, Q2.source, Q3.source, Q4.source, Q5.source, Q6.source
  N9: Q2.drain, J1.pin2
  N10: Q3.drain, J1.pin3
  N11: Q4.drain, J2.pin3
  N12: Q5.drain, J2.pin2
  N13: Q6.drain, J2.pin1
