# Fritzing sketch OfficeLighting (saved by Fritzing 0.9.1b)

parts:
  Part1 = Arduino Uno (Rev3)
  S1 = Pushbutton [package="[THT]"]
  S2 = Pushbutton [package="[THT]"]
  S3 = Pushbutton [package="[THT]"]
  S4 = Pushbutton [package="[THT]"]
  J1 = screw terminal, 3 pins
  C1 = Electrolytic Capacitor [capacitance=1mF package="100 mil [THT, electrolytic]"]
  R1 = Resistor [tolerance=±5% resistance=330 package=THT]

nets:
  N1: Part1.D2, S1.Pin_3, S1.Pin_4
  N2: Part1.D3_PWM, S2.Pin_3
  N3: Part1.D4, S3.Pin_3, S3.Pin_4
  N4: Part1.D5_PWM, S4.Pin_3, S4.Pin_4
  N5: Part1.D6_PWM, R1.Pin_1
  N6: Part1.GND, S1.Pin_2, S2.Pin_1, S2.Pin_2, S3.Pin_1, S3.Pin_2, S4.Pin_1, S4.Pin_2, J1.pin3, C1.-
  N7: Part1.VIN, J1.pin1, C1.+
  N8: J1.pin2, R1.Pin_0
